# Fritzing sketch HDD_solenoid_engine (saved by Fritzing 0.9.0b)
circuit board: 8.46667cm x 5.64444cm
perfboards: 1
breadboards: 1

parts:
  IC1 = L293D [package=THT]
  9v = Power plug
  C1 = Electrolytic Capacitor [capacitance=100nF voltage=16V package="100 mil [THT, electrolytic]"]
  C2 = Electrolytic Capacitor [capacitance=100nF voltage=16V package="100 mil [THT, electrolytic]"]
  J1 = Screw terminal - 2 pins [package=THT]
  U1 = Voltage Regulator - 5V [package="TO220 [THT]"]
  R1 = Resistor [tolerance=±5% resistance=750 package=THT]
  H1 = OH090U Hall effect sensor [package="TO92 [THT]"]
  stm32f407-DISCO_1 = female pin header, 10 pins [form="♀ (female)"]
  stm32f407-DISCO_2 = female pin header, 10 pins [form="♀ (female)"]

nets:
  Enable_1/PE6: IC1.Enable_1, stm32f407-DISCO_1.pin6
  Dir_1_B/PE3: IC1.In_1, stm32f407-DISCO_2.pin3
  Coil_A: IC1.Out_1_(_Controlled_by_Enable_1_), J1.pin1
  GND: IC1.0V, 9v.GND, C1.-, C2.-, U1.GND, H1.GND, stm32f407-DISCO_1.pin1, stm32f407-DISCO_2.pin10
  Coil_B: IC1.Out_2_(_Controlled_by_Enable_1_), J1.pin2
  Dir_1_A/PE1: IC1.In_2, stm32f407-DISCO_2.pin2
  Vmotor: IC1.+Vmotor, 9v.VCC, C1.+, U1.input_voltage
  +5v: IC1.+V, C2.+, U1.output_voltage, R1.Pin_0, H1.+Vs, stm32f407-DISCO_1.pin2, stm32f407-DISCO_2.pin9
  PE4/Sensor_A: R1.Pin_1, H1.Vout, stm32f407-DISCO_1.pin7
  PH0: stm32f407-DISCO_1.pin4
  PC14: stm32f407-DISCO_1.pin5
  PE2: stm32f407-DISCO_1.pin8
  PE0: stm32f407-DISCO_1.pin9
  PB8: stm32f407-DISCO_1.pin10
  PB9: stm32f407-DISCO_2.pin1
  PE5: stm32f407-DISCO_2.pin4
  PC13: stm32f407-DISCO_2.pin5
  PC15: stm32f407-DISCO_2.pin6
  PH1: stm32f407-DISCO_2.pin7

notes:
  Power supply
  STM32F407-DISCO
  Hall effect sensor
  Solenoid control
